# Fritzing sketch night_light (saved by Fritzing 0.9.3b)
breadboards: 1

parts:
  Часть1 = Arduino Uno (Rev3)
  S1 = Pushbutton [package="[THT]"]
  R1 = Resistor [tolerance=±5% resistance=220 package=THT]
  LED1 = RGB LED - (4 legs) [package="5 mm [THT]"]

nets:
  N1: Часть1.D9_PWM, LED1.green_cathode
  N2: Часть1.D10_PWM/SS, LED1.common_anode
  N3: Часть1.D11_PWM/MOSI, LED1.red_cathode
  N4: Часть1.D2, S1.Pin_1, S1.Pin_2, R1.Pin_0
  N5: Часть1.5V, S1.Pin_3, S1.Pin_4
  N6: Часть1.GND, R1.Pin_1

// code stored in the sketch: code_for_the_nightlight.ino
const int BLED=9;
const int GLED=10;
const int RLED=11;
const int BUTTON=2;
boolean lastButton = LOW;
boolean currentButton = LOW;
int ledMode = 0;
void setup ()
{
pinMode (BLED, OUTPUT);
pinMode (GLED, OUTPUT);
pinMode (RLED, OUTPUT);
pinMode (BUTTON, INPUT);
}
boolean debounce(boolean last)
{
boolean current = digitalRead(BUTTON);
if (last != current)
{
delay(5);
current = digitalRead(BUTTON);
return current;
}
}
void setMode(int mode)
{
// ???????
if (mode == 1)
{
digitalWrite(RLED, HIGH);
digitalWrite(GLED, LOW);
digitalWrite(BLED, LOW);
}
// ???????
else if (mode == 2)
{
digitalWrite(RLED, LOW);
digitalWrite(GLED, HIGH);
digitalWrite(BLED, LOW);
}
// ?????
else if (mode == 3)
{
digitalWrite(RLED, LOW);
digitalWrite(GLED, LOW);
digitalWrite(BLED, HIGH);
}
// ????????? (???????+ ?????)
else if (mode == 4)
{
analogWrite(RLED, 127);
analogWrite(GLED, 0);
analogWrite(BLED, 127);
}
// ????????? (?????+ ???????)
else if (mode == 5)
{
analogWrite(RLED, 0);
analogWrite(GLED, 127);
analogWrite(BLED, 127);
}
// ????????? (???????+ ???????)
else if (mode == 6)
{
analogWrite(RLED, 127);
analogWrite(GLED, 127);
analogWrite(BLED, 0);
}
// ????? (???????+ ???????+ ?????)
else if (mode == 7)
{
analogWrite(RLED, 85);
analogWrite(GLED, 85);
analogWrite(BLED, 85);
}
// ???????? (mode = 0)
else
{
digitalWrite(RLED, LOW);
digitalWrite(GLED, LOW);
digitalWrite(BLED, LOW);
}
}
void loop()
{
currentButton = debounce(lastButton);
if (lastButton == LOW && currentButton == HIGH)
{
ledMode++;
}
lastButton = currentButton;
if (ledMode == 8)
ledMode = 0;
setMode(ledMode);
}
